// Logisim project (A+B).(C+~D).circ as structural Verilog: 1 circuit, main circuit main
module main (
  input  A,
  input  B,
  input  C,
  input  D,
  output X
);

  wire not_1_out, or_1_out, or_2_out;

  not not_1 (not_1_out, D);
  or or_1 (or_1_out, A, B);
  or or_2 (or_2_out, C, not_1_out);
  and and_1 (X, or_1_out, or_2_out);
endmodule
